# Fritzing sketch CO2Ampel (saved by Fritzing 0.9.3b)
perfboards: 1

parts:
  Heltec_WiFi_LoRa_32_V1 = Heltec WiFi LoRa 32 V2 [part_number=HTIT-WB32LA]
  Neopixel = SMD RGB LED (WS2812) [package=5050]
  MH-Z19B = MH-Z19 CO2 sensor [part_number=MH-Z19]
  BME680 = Adafruit BME680 [part_number="Adafruit #3660"]
  U1 = BUTTON-CONDUCTIVE [package=button-conductive-mini]

nets:
  N1: Heltec_WiFi_LoRa_32_V1.pin_1, BME680.VCC, BME680.SDI/SDA
  N2: Heltec_WiFi_LoRa_32_V1.pin_2, U1.2
  N3: Heltec_WiFi_LoRa_32_V1.pin_7, Neopixel.DIn
  N4: Heltec_WiFi_LoRa_32_V1.pin_16, Heltec_WiFi_LoRa_32_V1.pin_17, BME680.3.3V
  VSS: Heltec_WiFi_LoRa_32_V1.pin_18, Heltec_WiFi_LoRa_32_V1.pin_19, Neopixel.VSS, BME680.GND, U1.1
  VCC: Heltec_WiFi_LoRa_32_V1.pin_20, Neopixel.VCC, MH-Z19B.Vin
  N5: Heltec_WiFi_LoRa_32_V1.pin_21, Heltec_WiFi_LoRa_32_V1.pin_22
  N6: Heltec_WiFi_LoRa_32_V1.pin_23, MH-Z19B.RX
  N7: Heltec_WiFi_LoRa_32_V1.pin_24, MH-Z19B.TX
  N8: Heltec_WiFi_LoRa_32_V1.pin_27, BME680.SCK/SCL

custom parts:
  Heltec WiFi LoRa 32 V2: Heltec WiFi LoRa 32 V2 WiFi LoRa 32 is a classic IoT dev-board designed & produced by Heltec Automation(TM). It’s a highly integrated product based on ESP32 + SX127x, it has Wi-Fi, BLE, LoRa functions, also Li-Po battery management system, 0.96″ OLED are also included. It’s the best choice for smart cities, smart farms, smart home, and IoT makers.
