# Fritzing sketch CO2-Ampel_Amica (saved by Fritzing 0.9.3b)

parts:
  M1 = BME680 Module [part_number=CJMCU-680]
  U1 = NodeMCU V1.0
  TD-er1 = MH-Z19 CO2 sensor [part_number=MH-Z19]
  OLED_I2C1 = OLED 128x64 I2C Monochrome Display
  Bauteil1 = NeoPixel Stick [part_number=1426]
  3V_/_5V_Batterie_board_(5V_out)) = 18650 battery holder [package=battery-18650-kit]

nets:
  VCC: M1.VCC, U1.3V3, OLED_I2C1.VDD, Bauteil1.+5V
  GND: M1.GND, U1.GND, TD-er1.GND, OLED_I2C1.GND, Bauteil1.GND, 3V_/_5V_Batterie_board_(5V_out)).-
  N1: M1.SCL, U1.D1, OLED_I2C1.SCK
  N2: M1.SDA, U1.D2, OLED_I2C1.SDA
  N3: U1.D4, Bauteil1.DATAIN
  N4: U1.D6, TD-er1.RX
  N5: U1.D7, TD-er1.TX
  VIN: U1.Vin, TD-er1.Vin, 3V_/_5V_Batterie_board_(5V_out)).+

custom parts:
  BME680 Module: Bosch BME680 Development Module The BME680 is a digital 4-in-1 sensor that measures air quality [gas], humidity, pressure and temperature. Links: BME680 product datasheet
  NodeMCU V1.0: ESP8266 based NodeMCU
  NeoPixel Stick: Make your own little LED strip arrangement with this stick of NeoPixel LEDs. We crammed 8 of the tiny 5050 (5mm x 5mm) smart RGB LEDs onto a PCB with mounting holes and a chainable design. Use only one microcontroller pin to control as many as you can chain together! Each LED is addressable as the driver chip is inside the LED. Each one has ~18mA constant current drive so the color will be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
  18650 battery holder: 18650 Battery Holder
