# Fritzing sketch CO2-Ampel_Anschluss_Esp8266-BME680 (saved by Fritzing 0.9.3b)

parts:
  Amica = NodeMCU V1.0
  BME680 = BME680 Module [part_number=CJMCU-680]

nets:
  N1: Amica.D1, BME680.SCL
  N2: Amica.D2, BME680.SDA
  3V3: Amica.3V3, BME680.VCC
  GND: Amica.GND, BME680.GND

custom parts:
  NodeMCU V1.0: ESP8266 based NodeMCU
  BME680 Module: Bosch BME680 Development Module The BME680 is a digital 4-in-1 sensor that measures air quality [gas], humidity, pressure and temperature. Links: BME680 product datasheet
