# Fritzing sketch CO2-Ampel_Anschluss_Esp8266-MH-Z19b (saved by Fritzing 0.9.3b)

parts:
  Amica = NodeMCU V1.0
  CO2 = MH-Z19 CO2 sensor [part_number=MH-Z19]

nets:
  N1: Amica.D6, CO2.RX
  N2: Amica.D7, CO2.TX
  VIN: Amica.Vin, CO2.Vin
  GND: Amica.GND, CO2.GND

custom parts:
  NodeMCU V1.0: ESP8266 based NodeMCU
