# Fritzing sketch CO2-Ampel_Anschluss_Esp8266-SSD1306 (saved by Fritzing 0.9.3b)

parts:
  Amica = NodeMCU V1.0
  OLED_I2C1 = OLED 128x64 I2C Monochrome Display

nets:
  N1: Amica.D1, OLED_I2C1.SCK
  N2: Amica.D2, OLED_I2C1.SDA
  3V3: Amica.3V3, OLED_I2C1.VDD
  GND: Amica.GND, OLED_I2C1.GND

custom parts:
  NodeMCU V1.0: ESP8266 based NodeMCU
