# Fritzing sketch CO2-Ampel_Anschluss_Esp8266Neopixel- (saved by Fritzing 0.9.3b)

parts:
  Amica = NodeMCU V1.0
  Neopixel_/_WS2812b = NeoPixel Stick [part_number=1426]

nets:
  N1: Amica.D4, Neopixel_/_WS2812b.DATAIN
  GND: Amica.GND, Neopixel_/_WS2812b.GND
  3V3: Amica.3V3, Neopixel_/_WS2812b.+5V

custom parts:
  NodeMCU V1.0: ESP8266 based NodeMCU
  NeoPixel Stick: Make your own little LED strip arrangement with this stick of NeoPixel LEDs. We crammed 8 of the tiny 5050 (5mm x 5mm) smart RGB LEDs onto a PCB with mounting holes and a chainable design. Use only one microcontroller pin to control as many as you can chain together! Each LED is addressable as the driver chip is inside the LED. Each one has ~18mA constant current drive so the color will be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
